# Fritzing sketch POV (saved by Fritzing 0.8.7b)
circuit board: 8.08cm x 3cm
breadboards: 2

parts:
  IC1 = TLC5947 [chip_label=IC package="HTSSOP-32 Power Pad"]
  LED1 = Super Flux RGB LED (com. anode)
  LED2 = Super Flux RGB LED (com. anode)
  LED3 = Super Flux RGB LED (com. anode)
  LED4 = Super Flux RGB LED (com. anode)
  LED5 = Super Flux RGB LED (com. anode)
  LED6 = Super Flux RGB LED (com. anode)
  LED7 = Super Flux RGB LED (com. anode)
  LED8 = Super Flux RGB LED (com. anode)
  In = male pin header, 6 pins [form="♂ (male)"]
  R1 = Resistor [tolerance=±5% resistance=2.2k package=THT]
  C1 = Electrolytic Capacitor [capacitance=1mF package="100 mil [THT, electrolytic]"]
  OUT = male pin header, 6 pins [form="♂ (male)"]
  Bauteil1 = Arduino Uno (Rev3)
  Power_plug1 = Power plug
  U1 = EM406 GPS Connector [package=em406]
  RHT1 = Humidity and Temperature Sensor RHT03
  R2 = Resistor [tolerance=±5% resistance=10k package=THT]
  U3 = HALL-EFFECT [package=sc70]

nets:
  GND: IC1.1, IC1.2, In.pin4, In.pin6, R1.Pin_0, C1.-, OUT.pin4, OUT.pin6, Bauteil1.GND, Power_plug1.GND, U1.GND1, RHT1.GND_2, U3.GND
  N1: IC1.3, In.pin2, OUT.pin2, Bauteil1.D9_PWM
  N2: IC1.4, In.pin1, Bauteil1.D10_PWM/SS
  N3: IC1.5, LED1.red_cathode
  N4: IC1.6, LED1.green_cathode
  N5: IC1.7, LED1.blue_cathode
  N6: IC1.8, LED2.red_cathode
  N7: IC1.9, LED2.green_cathode
  N8: IC1.10, LED2.blue_cathode
  N9: IC1.11, LED3.red_cathode
  N10: IC1.12, LED3.green_cathode
  N11: IC1.13, LED3.blue_cathode
  N12: IC1.14, LED4.red_cathode
  N13: IC1.15, LED4.green_cathode
  N14: IC1.16, LED4.blue_cathode
  N15: IC1.17, LED5.red_cathode
  N16: IC1.18, LED5.green_cathode
  N17: IC1.19, LED5.blue_cathode
  N18: IC1.20, LED6.red_cathode
  N19: IC1.21, LED6.green_cathode
  N20: IC1.22, LED6.blue_cathode
  N21: IC1.23, LED7.red_cathode
  N22: IC1.24, LED7.green_cathode
  N23: IC1.25, LED7.blue_cathode
  N24: IC1.26, LED8.red_cathode
  N25: IC1.27, LED8.green_cathode
  N26: IC1.28, LED8.blue_cathode
  N27: IC1.29, OUT.pin1
  N28: IC1.30, In.pin3, OUT.pin3, Bauteil1.D8
  N29: IC1.31, R1.Pin_1
  VCC: IC1.32, LED1.common_anode, LED2.common_anode, LED3.common_anode, LED4.common_anode, LED5.common_anode, LED6.common_anode, LED7.common_anode, LED8.common_anode, In.pin5, C1.+, OUT.pin5, Bauteil1.5V, Power_plug1.VCC, U1.VCC, RHT1.Vcc, R2.Pin_0, U3.VCC
  N30: Bauteil1.D0/RX, U1.RX
  N31: Bauteil1.D1/TX, U1.TX
  N32: Bauteil1.D2, U3.OUT
  N33: Bauteil1.D4, RHT1.Data-signal, R2.Pin_1

notes:
  OUT
  IN
  1
  2
  3
  4
  5
  6
  7
  8
  SIN
  SCLK
  XLAT
  BLANK
  VCC
  GND
  SOUT
  LED Board V2 Ping Gruppe M5
  Design: Maximilian Junk
